# Fritzing sketch MultiplexerCircuit (saved by Fritzing 0.9.9b)
breadboards: 1

parts:
  Part1 = Arduino Uno (Rev3)
  Part2 = Analog Digital MUX Breakout
  S1 = SWITCH-MOMENTARY-2 [package=reed_switch_plastic]
  R1 = Resistor [tolerance=±5% power=0.25 resistance=10k package=THT]
  S2 = SWITCH-MOMENTARY-2 [package=reed_switch_plastic]
  S3 = SWITCH-MOMENTARY-2 [package=reed_switch_plastic]
  S4 = SWITCH-MOMENTARY-2 [package=reed_switch_plastic]
  S5 = SWITCH-MOMENTARY-2 [package=reed_switch_plastic]
  S6 = SWITCH-MOMENTARY-2 [package=reed_switch_plastic]
  S7 = SWITCH-MOMENTARY-2 [package=reed_switch_plastic]
  S8 = SWITCH-MOMENTARY-2 [package=reed_switch_plastic]
  S9 = SWITCH-MOMENTARY-2 [package=reed_switch_plastic]
  S10 = SWITCH-MOMENTARY-2 [package=reed_switch_plastic]
  S11 = SWITCH-MOMENTARY-2 [package=reed_switch_plastic]
  S12 = SWITCH-MOMENTARY-2 [package=reed_switch_plastic]
  S13 = SWITCH-MOMENTARY-2 [package=reed_switch_plastic]
  S14 = SWITCH-MOMENTARY-2 [package=reed_switch_plastic]
  S15 = SWITCH-MOMENTARY-2 [package=reed_switch_plastic]
  S16 = SWITCH-MOMENTARY-2 [package=reed_switch_plastic]
  R2 = Resistor [tolerance=±5% power=0.25 resistance=10k package=THT]
  R3 = Resistor [tolerance=±5% power=0.25 resistance=10k package=THT]
  R4 = Resistor [tolerance=±5% power=0.25 resistance=10k package=THT]
  R5 = Resistor [tolerance=±5% power=0.25 resistance=10k package=THT]
  R6 = Resistor [tolerance=±5% power=0.25 resistance=10k package=THT]
  R7 = Resistor [tolerance=±5% power=0.25 resistance=10k package=THT]
  R8 = Resistor [tolerance=±5% power=0.25 resistance=10k package=THT]
  R9 = Resistor [tolerance=±5% power=0.25 resistance=10k package=THT]
  R10 = Resistor [tolerance=±5% power=0.25 resistance=10k package=THT]
  R11 = Resistor [tolerance=±5% power=0.25 resistance=10k package=THT]
  R12 = Resistor [tolerance=±5% power=0.25 resistance=10k package=THT]
  R13 = Resistor [tolerance=±5% power=0.25 resistance=10k package=THT]
  R14 = Resistor [tolerance=±5% power=0.25 resistance=10k package=THT]
  R15 = Resistor [tolerance=±5% power=0.25 resistance=10k package=THT]
  R16 = Resistor [tolerance=±5% power=0.25 resistance=10k package=THT]

nets:
  N1: Part1.D8, Part2.S0
  N2: Part1.D9_PWM, Part2.S1
  N3: Part1.D10_PWM/SS, Part2.S2
  N4: Part1.D11_PWM/MOSI, Part2.S3
  N5: Part1.D3_PWM, Part2.SIG
  5V: Part1.5V, Part2.VCC, S1.1, S2.1, S3.1, S4.1, S5.1, S6.1, S7.1, S8.1, S9.1, S10.1, S11.1, S12.1, S13.1, S14.1, S15.1, S16.1
  GND: Part1.GND, Part2.GND, R1.Pin_1, R2.Pin_1, R3.Pin_1, R4.Pin_1, R5.Pin_1, R6.Pin_1, R7.Pin_1, R8.Pin_1, R9.Pin_0, R10.Pin_0, R11.Pin_0, R12.Pin_0, R13.Pin_0, R14.Pin_0, R15.Pin_0, R16.Pin_1
  N6: Part2.C0, S1.2, R1.Pin_0
  N7: Part2.C1, S2.2, R2.Pin_0
  N8: Part2.C2, S3.2, R3.Pin_0
  N9: Part2.C3, S8.2, R4.Pin_0
  N10: Part2.C4, S6.2, R5.Pin_0
  N11: Part2.C5, S5.2, R6.Pin_0
  N12: Part2.C7, S16.2, R8.Pin_0
  N13: Part2.C8, S4.2, R9.Pin_1
  N14: Part2.C9, S7.2, R10.Pin_1
  N15: Part2.C10, S10.2, R11.Pin_1
  N16: Part2.C11, S11.2, R12.Pin_1
  N17: Part2.C12, S12.2, R13.Pin_1
  N18: Part2.C13, S13.2, R14.Pin_1
  N19: Part2.C14, S14.2, R15.Pin_1
  N20: Part2.C15, S15.2, R16.Pin_0
  N21: S9.2, R7.Pin_0
